# Fritzing sketch scheme-a (saved by Fritzing 0.8.7b)
breadboards: 1

parts:
  LCD1 = LCD screen
  Mod1 = Raspberry Pi 4B
  RE1 = Rotary Encoder [package=THT]

nets:
  VSS: LCD1.VSS, LCD1.LED-, Mod1.GND, Mod1.GPIO14, RE1.EncoderPinB
  VDD: LCD1.VDD, LCD1.LED+, Mod1.5V, RE1.EncoderPinA
  N1: LCD1.V0, RE1.EncoderPinC
  N2: LCD1.RS, Mod1.GPIO2
  N3: LCD1.R/W, Mod1.GPIO3
  N4: LCD1.E, Mod1.GPIO4
  N5: LCD1.DB4, Mod1.GPIO8
  N6: LCD1.DB5, Mod1.GPIO7
  N7: LCD1.DB6, Mod1.GPIO6
  N8: LCD1.DB7, Mod1.GPIO5
